# Fritzing sketch esp-gatecontrol-garage-unit (saved by Fritzing 0.9.3b)

parts:
  Bauteil1 = Arduino Uno (Rev3)
  S1 = Reed switch [package=THT]
  HC-1 = HC-12 Module
  R1 = Resistor [tolerance=±5% resistance=10k package="0603 [SMD]"]
  R2 = Resistor [tolerance=±5% resistance=10k package="0603 [SMD]"]
  KY-1 = Keyes Relay [package=THT]
  KY-2 = Keyes Relay [package=THT]
  S2 = Reed switch [package=THT]

nets:
  N1: Bauteil1.D8, KY-2.signal
  N2: Bauteil1.D9_PWM, S1.pin_1, R2.Pin_1
  N3: Bauteil1.D10_PWM/SS, R1.Pin_1
  GND: Bauteil1.GND, HC-1.GND, R1.Pin_0, R2.Pin_0, KY-1.ground, KY-2.ground
  N4: Bauteil1.D5_PWM, HC-1.RXD
  N5: Bauteil1.D6_PWM, HC-1.TXD
  N6: Bauteil1.D7, KY-1.signal
  3V3: Bauteil1.3V3, S1.pin_2, HC-1.VCC, KY-1.power, KY-2.power, S2.pin_2

notes:
  Pull-Down Widerstände

custom parts:
  HC-12 Module: HC-12 433Mhz Module
  Keyes Relay: The Keyes 5V relay module is suitable for SCM development, home appliance control. It uses a 5V~12V TIL control signal which can control DC / AC signal.
